// Logisim project Conway.circ as structural Verilog: 1 circuit, main circuit main
module main (
  input  NE2,
  input  E3,
  input  Clock,
  input  Row,
  input  Column,
  input  Lock
);

  wire and_2_out, and_3_out, and_4_out, and_5_out, Btn_Invert_out, D_In_qn, D_Out_q, not_1_out, or_1_out;

  Button Btn_Invert (.out(Btn_Invert_out));
  // AND_Gate and_1 has open pins: in0=Row, in1=Column, out=open
  not not_1 (not_1_out, Lock);
  and and_2 (and_2_out, not_1_out, Btn_Invert_out);
  and and_3 (and_3_out, Clock, not_1_out);
  and and_4 (and_4_out, and_3_out, Btn_Invert_out);
  and and_5 (and_5_out, and_2_out, D_In_qn);
  D_Flip_Flop D_In (.D(and_5_out), .clk(and_4_out), .Qn(D_In_qn));  // open: Q, preset, reset
  buf or_1 (or_1_out, Clock);  // OR_Gate
  D_Flip_Flop D_Out (.clk(or_1_out), .Q(D_Out_q));  // open: D, Qn, preset, reset
  LED led_1 (.in(D_Out_q));
endmodule
